# Fritzing sketch main (saved by Fritzing 0.9.4)

parts:
  SW1 = Rotary_encoder [package=encoder_led_3]
  SW2 = Rotary_encoder [package=encoder_led_3]
  SW3 = Rotary_encoder [package=encoder_led_3]
  U4 = Slide_potentiometer_10k [package=slider]
  U5 = Slide_potentiometer_10k [package=slider]
  U6 = Slide_potentiometer_10k [package=slider]
  Pro_Micro1 = SparkFun Pro Micro
  S1 = Round Pushbutton
  S2 = Round Pushbutton
  S3 = Round Pushbutton
  S4 = Round Pushbutton
  S5 = Round Pushbutton
  S6 = Round Pushbutton  # not connected
  S7 = Round Pushbutton
  S8 = Round Pushbutton  # not connected
  S9 = Round Pushbutton  # not connected
  S10 = Round Pushbutton  # not connected
  S11 = Round Pushbutton  # not connected
  S12 = Round Pushbutton  # not connected
  S13 = Round Pushbutton  # not connected
  S14 = Round Pushbutton  # not connected
  S15 = Round Pushbutton  # not connected
  S16 = Round Pushbutton  # not connected
  Part1 = Analog Digital MUX Breakout
  IC2 = MC14490P [package="DIP16 [THT]"]
  C1 = Capacitor [package=cap-pth-small2]
  IC3 = MC14490P [package="DIP16 [THT]"]
  C2 = Capacitor [package=cap-pth-small2]

nets:
  N1: SW1.CLK, Pro_Micro1.9
  N2: SW1.DT, Pro_Micro1.8
  N3: SW1.SW, Pro_Micro1.7
  VCC: SW1.+, SW2.+, SW3.+, U4.VCC, U5.VCC, U6.VCC, Pro_Micro1.VCC, Part1.VCC, IC3.VDD
  GND: SW1.GND, SW2.GND, SW3.GND, U4.GND, U5.GND, U6.GND, Pro_Micro1.GND, S1.leg1, Part1.GND, Part1.EN, IC3.Vss
  N4: SW2.CLK, Pro_Micro1.6
  N5: SW2.SW, Pro_Micro1.5
  N6: SW3.CLK, Pro_Micro1.3
  N7: SW3.DT, Pro_Micro1.2
  N8: SW3.SW, Pro_Micro1.RX1
  N9: U4.OTB, Pro_Micro1.A0
  N10: U5.OTB, Pro_Micro1.A1
  N11: U6.OTB, Pro_Micro1.A2
  N12: Pro_Micro1.10, Part1.S0
  N13: Pro_Micro1.16, Part1.S1
  N14: Pro_Micro1.14, Part1.S2
  N15: Pro_Micro1.15, Part1.S3
  N16: Pro_Micro1.A3, Part1.SIG
  N17: S1.leg0, IC2.Aout
  N18: S2.leg0, IC2.Bout
  N19: S3.leg0, IC2.Cout
  N20: S4.leg0, IC2.Eout
  N21: S5.leg0, IC2.Fout
  N22: S7.leg0, IC2.Dout
  N23: Part1.C0, IC2.Ain
  N24: Part1.C1, IC2.Bin
  N25: Part1.C2, IC2.Cin
  N26: Part1.C3, IC2.Din
  N27: Part1.C4, IC2.Ein
  N28: Part1.C5, IC2.Fin
  N29: Part1.C6, IC3.Ain
  N30: Part1.C7, IC3.Bin
  N31: Part1.C8, IC3.Cin
  N32: Part1.C9, IC3.Din
  N33: Part1.C10, IC3.Fin
  N34: IC2.OSCin, C1.2
  N35: IC2.OSCout, C1.1
  N36: IC3.OSCin, C2.2
  N37: IC3.OSCout, C2.1

custom parts:
  Rotary_encoder: 360 Degrees Rotary Encoder Module For Arduino
  Slide_potentiometer_10k: Slide Potentiometer 10K Linear Module Dual Output for Arduino AVR Electronic Block
  SparkFun Pro Micro: The Pro Micro is similar to the Pro Mini except with an ATmega32U4 on board. The USB transceiver inside the 32U4 allows us to add USB connectivity on-board and do away with bulky external USB interface. Based on: https://github.com/unorthodox-engineers/unorthodox-arduino/blob/master/Unorthodox/fritzing/parts/Pro%20Micro.fzpz
  MC14490P: MC14490P DIP-16 MC14490 DIP16 MC14490PG DIP logic chip hardware debouncer
